// Digital circuit CPU.dig as structural Verilog
module CPU (
  input  clk,
  input  CLR_PC
);

  wire comparator_1_eq, comparator_2_eq, comparator_3_eq, comparator_4_eq, comparator_5_eq, comparator_6_eq,
       comparator_7_eq, comparator_8_eq, comparator_9_eq;
  wire [7:0] programme_counter_1_p1, rom_1_d;
  wire [15:0] programme_counter_1_p2, programme_counter_1_p7;

  Comparator #(.Bits(8)) comparator_1 (.a(rom_1_d), .b(8'h1), .eq(comparator_1_eq));  // open: gt, lt
  Comparator #(.Bits(8)) comparator_2 (.a(rom_1_d), .b(8'h2), .eq(comparator_2_eq));  // open: gt, lt
  Comparator #(.Bits(8)) comparator_3 (.a(rom_1_d), .b(8'h1), .eq(comparator_3_eq));  // open: gt, lt
  Comparator #(.Bits(8)) comparator_4 (.a(rom_1_d), .b(8'h1), .eq(comparator_4_eq));  // open: gt, lt
  Comparator #(.Bits(8)) comparator_5 (.a(rom_1_d), .b(8'h1), .eq(comparator_5_eq));  // open: gt, lt
  Comparator #(.Bits(8)) comparator_6 (.a(rom_1_d), .b(8'h1), .eq(comparator_6_eq));  // open: gt, lt
  Comparator #(.Bits(8)) comparator_7 (.a(rom_1_d), .b(8'h1), .eq(comparator_7_eq));  // open: gt, lt
  Comparator #(.Bits(8)) comparator_8 (.a(rom_1_d), .b(8'h1), .eq(comparator_8_eq));  // open: gt, lt
  Comparator #(.Bits(8)) comparator_9 (.a(rom_1_d), .b(8'h1), .eq(comparator_9_eq));  // open: gt, lt
  // Programme_Counter programme_counter_1: pin names not known; wires that end beside it: programme_counter_1_p1, programme_counter_1_p2, clk, comparator_1_eq, comparator_2_eq, CLR_PC, programme_counter_1_p7
  ALU alu_1 (.CMD(rom_1_d), .DAT(programme_counter_1_p1), .CLK(clk), .Q(programme_counter_1_p1));
  ROM #(.AddrBits(16), .Bits(8)) rom_1 (.A(programme_counter_1_p7), .sel(1'b1), .D(rom_1_d));
  ROM #(.AddrBits(16), .Bits(8)) rom_2 (.A(programme_counter_1_p7), .sel(1'b1), .D(programme_counter_1_p1));
  ROM #(.AddrBits(16), .Bits(16)) rom_3 (.A(programme_counter_1_p7), .sel(1'b1), .D(programme_counter_1_p2));
  // RAM ram_1: pin names not known; wires that end beside it: programme_counter_1_p1, programme_counter_1_p2, comparator_3_eq, comparator_4_eq, comparator_5_eq, comparator_6_eq, comparator_7_eq, comparator_8_eq, comparator_9_eq, clk, programme_counter_1_p1, programme_counter_1_p2

  // Notes on the sheet:
  //   clk: Hz: 10
  //   LN
  //   LN: output from the programmme counter,
  //   the current line of code being executed
  //   DAT
  //   CMD
  //   ADR
  //   CLK
  //   - Flash memory
endmodule
